# Fritzing sketch Modular_Schematic (saved by Fritzing 0.9.3b)

parts:
  Part1 = Adafruit VL53L0X Time of Flight Distance Sensor [part_number="Adafruit #3317"]
  U1 = Voltage Regulator [package=to220-adj]
  U2 = LIPO-110mAh [part_number=Lipo package=lipo-110]
  U3 = LIPO-110mAh [package=lipo-110]
  R1 = Resistor [tolerance=±5% resistance=330 package="0805 [SMD]"]
  R2 = Resistor [tolerance=±5% resistance=1.2k package="0805 [SMD]"]
  Part2 = Arduino Nano (Rev3.0)
  Part3 = NRF24L01+ Breakout Board
  Part4 = Bluetooth HC-05 Macho
  S1 = Pushbutton [package="[SMD]"]
  Male = Basic Servo
  Female = Basic Servo
  Base = Basic Servo
  Left = Basic Servo
  Right = Basic Servo

nets:
  VIN: Part1.VIN, Part2.5V, Part4.VCC
  GND: Part1.GND, U3.-, R2.Pin_0, Part2.GND, Part3.GND, Part4.GND, Male.gnd, Female.gnd, Base.gnd, Left.gnd, Right.gnd
  N1: Part1.SCL, Part2.A5
  N2: Part1.SDA, Part2.A4
  N3: U1.ADJ, R1.Pin_1, R2.Pin_1
  N4: U1.IN, Part2.VIN, S1.Pin_1, S1.Pin_2
  VCC: U1.OUT, R1.Pin_0, Male.vcc, Female.vcc, Base.vcc, Left.vcc, Right.vcc
  N5: U2.+, S1.Pin_3, S1.Pin_4
  N6: U2.-, U3.+
  N7: Part2.D2, Part3.CE
  N8: Part2.D3, Right.pulse
  N9: Part2.D4, Part3.CS
  N10: Part2.D5, Female.pulse
  N11: Part2.D6, Male.pulse
  N12: Part2.D7, Part4.TXD
  N13: Part2.D8, Part4.RXD
  N14: Part2.D9, Left.pulse
  N15: Part2.D10, Base.pulse
  N16: Part2.D11/MOSI, Part3.MOSI
  N17: Part2.D12/MISO, Part3.MISO
  3V3: Part2.3V3, Part3.VCC
  N18: Part2.D13/SCK, Part3.SCK

notes:
  SCHEMATIC DIAGRAM

custom parts:
  Adafruit VL53L0X Time of Flight Distance Sensor: The VL53L0X is a Time of Flight distance sensor like no other you've used! The sensor contains a very tiny invisible laser source, and a matching sensor. The VL53L0X can detect the "time of flight", or how long the light has taken to bounce back to the sensor. Since it uses a very narrow light source, it is good for determining distance of only the surface directly in front of it. Unlike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
