# Fritzing sketch Task2_Servo-3_Nano_HC05 (saved by Fritzing 0.9.3b)

parts:
  Part1 = Arduino Nano (Rev3.0)
  SG-90(S1) = Basic Servo
  SG-90(S2) = Basic Servo
  SG-90(S3) = Basic Servo
  Part3 = Bluetooth HC-05 Macho
  U1 = LIPO-110mAh [package=lipo-110]
  U2 = LIPO-110mAh [package=lipo-110]
  J1 = Infrared Proximity Sensor
  Part4 = Adafruit VL53L0X Time of Flight Distance Sensor [part_number="Adafruit #3317"]

nets:
  N1: Part1.D1/TX, Part3.TXD
  N2: Part1.D0/RX, Part3.RXD
  GND: Part1.GND, Part3.GND, U2.-, J1.GND
  N3: Part1.D7, SG-90(S1).pulse
  N4: Part1.D8, SG-90(S2).pulse
  N5: Part1.D9, SG-90(S3).pulse
  N6: Part1.VIN, U1.+
  VCC: Part1.5V, Part3.VCC, J1.Vcc
  N7: Part1.A5, Part4.SCL
  N8: Part1.A4, Part4.SDA
  N9: Part1.A0, J1.Vout
  GND_2: SG-90(S1).gnd, SG-90(S2).gnd, SG-90(S3).gnd
  VCC_2: SG-90(S1).vcc, SG-90(S2).vcc, SG-90(S3).vcc
  N10: U1.-, U2.+

notes:
  Interfacing Arduino Nano with Servo SG90, Bluetooth module HC-05, Sharp IR and VL53L0X ToF
  ranging sensor

custom parts:
  Adafruit VL53L0X Time of Flight Distance Sensor: The VL53L0X is a Time of Flight distance sensor like no other you've used! The sensor contains a very tiny invisible laser source, and a matching sensor. The VL53L0X can detect the "time of flight", or how long the light has taken to bounce back to the sensor. Since it uses a very narrow light source, it is good for determining distance of only the surface directly in front of it. Unlike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
