# Fritzing sketch Config_Bluetooth_ATComm(Master Config) (saved by Fritzing 0.9.3b)

parts:
  MASTER = Bluetooth HC-05 Macho
  FT232 = FTDI Basic Programmer
  SLAVE = Bluetooth HC-05 Macho

nets:
  N1: MASTER.TXD, FT232.RXI
  N2: MASTER.RXD, FT232.TXO
  VCC: MASTER.VCC, FT232.POWER, SLAVE.VCC
  GND: MASTER.GND, FT232.GND, SLAVE.GND

notes:
  HC-05 interfacing with FT232
  (Master Config)
