# Fritzing sketch Config_Bluetooth_ATComm(Slave Config) (saved by Fritzing 0.9.3b)

parts:
  SLAVE = Bluetooth HC-05 Macho
  FT232 = FTDI Basic Programmer

nets:
  N1: SLAVE.TXD, FT232.RXI
  N2: SLAVE.RXD, FT232.TXO
  N3: SLAVE.VCC, FT232.POWER
  GND: SLAVE.GND, FT232.GND

notes:
  HC-05 interfacing with FT232
  (Slave Config)
